# Fritzing sketch schmatic (saved by Fritzing 0.9.9b)

parts:
  DHT1 = DHT22 Humidity and Temperature Sensor
  e-radionica_com1 = LM393 LDR breakout [part_number=100027]
  U3 = ESP8266 NodeMCU LoLin base
  2_Channel_Relay1 = 2 Channel Power Relay
  F1 = Fan - Ventilador [package=THT]
  LED2 = LEDs [package=led10mm]
  J1 = 2.1mm Barrel Jack with Terminal Block

nets:
  VCC: DHT1.VDD, e-radionica_com1.VCC, U3.3V2-0, U3.3V2-1, U3.3V2-2, U3.3V3-0, U3.3V3-1, 2_Channel_Relay1.VCC
  N1: DHT1.DATA, U3.D5-0, U3.D5-1
  GND: DHT1.GND, e-radionica_com1.GND, U3.GND1-3, U3.GND2-0, U3.GND2-1, U3.GND2-2, U3.GND3-0, U3.GND3-1, 2_Channel_Relay1.GND#11
  N2: e-radionica_com1.AO, U3.A0
  N3: U3.D6-0, U3.D6-1, U3.D6-2, 2_Channel_Relay1.IN1
  N4: U3.D7-0, U3.D7-1, 2_Channel_Relay1.IN2
  N5: 2_Channel_Relay1.JD-VCC, 2_Channel_Relay1.GND#10
  N6: 2_Channel_Relay1.K1-COM, LED2.C
  N7: 2_Channel_Relay1.K1-NO, 2_Channel_Relay1.K2-NO, J1.POS
  N8: 2_Channel_Relay1.K2-COM, F1.5V
  N9: F1.GND, LED2.A, J1.NEG

notes:
  Power eksternal 12/5V
  DHT 22
  Relay 2 channel 5v
  LDR
  NodeMCU + expansion board
  Fan 12v
  Lampu pijar

custom parts:
  ESP8266 NodeMCU LoLin base: ESP8266 based NodeMCU Base
  2 Channel Power Relay: A 2 channel power relay. The module operates at 5V.
  Fan - Ventilador: Ventilador de 2 pines, se encuentra comunmente en computadoras de escritorio
  LEDs: LEDs Standard schematic elements and footprints for 5mm, 3mm, 1206, and 0603 sized LEDs. 5mm - Spark Fun Electronics SKU : COM-00529 (and others)
